# Fritzing sketch MORSE (saved by Fritzing 0.9.4)

parts:
  R1 = Resistor [tolerance=±5% resistance=220 package=THT]
  LED1 = LED - 5mm [color="Red (633nm)" package="5 mm [THT]"]
  Touch_Sensor = mystery part, 3 pins [chip_label=?]
  Part1 = Arduino Nano (Rev3.0)
  VCC1 = Battery block 9V

nets:
  N1: R1.Pin_0, Part1.D4
  N2: R1.Pin_1, LED1.anode
  N3: LED1.cathode, Touch_Sensor.pin3, Part1.GND, VCC1.-
  N4: Touch_Sensor.pin1, Part1.5V
  N5: Touch_Sensor.pin2, Part1.D3
  N6: Part1.VIN, VCC1.+
