# Fritzing sketch morse (saved by Fritzing 0.9.4)
breadboards: 2

parts:
  Part1 = Arduino Uno (Rev3)
  LED1 = LED - 5mm [color="Red (633nm)" package="5 mm [THT]"]
  R1 = Resistor [tolerance=±5% resistance=220 package=THT]
  Part2 = Arduino Uno (Rev3)
  LED2 = LED - 5mm [color="Red (633nm)" package="5 mm [THT]"]
  R2 = Resistor [tolerance=±5% resistance=220 package=THT]
  Part3 = Bluetooth HC-05 Macho

nets:
  N1: Part1.D4, R1.Pin_1
  N2: Part1.GND, LED1.cathode
  N3: LED1.anode, R1.Pin_0
  N4: Part2.D0/RX, Part3.TXD
  N5: Part2.D1/TX, Part3.RXD
  N6: Part2.D4, R2.Pin_1
  3V3: Part2.3V3, Part3.VCC
  GND: Part2.GND, LED2.cathode, Part3.GND
  N7: LED2.anode, R2.Pin_0

notes:
  Serial Schematic
  BLE Schematic
